# Fritzing sketch velociruabtor_v2 (saved by Fritzing 0.9.3b)
circuit board: 12.4853cm x 7.494cm

parts:
  Componente1 = Triple Axis Accelerometer Breakout - ADXL335
  Teensy_3_1 = Teensy 3.1
  Componente2 = Bluetooth HC-05 Macho
  Componente3 = Motor Driver 1A Dual TB6612FNG
  S1 = Pololu QTR-8 Reflectabce Sensor array [package=THT]

nets:
  N1: Componente1.ZOUT, Teensy_3_1.A2/D16
  N2: Componente1.YOUT, Teensy_3_1.A1/D15
  N3: Componente1.XOUT, Teensy_3_1.A0/D14
  GND: Componente1.GND, Teensy_3_1.GND, Componente2.GND, Componente3.GND, S1.pin1, S1.pin15, S1.pin18
  VCC: Componente1.VCC, Teensy_3_1.3V3, Componente2.VCC, Componente3.VCC, S1.pin14, S1.pin22
  N4: Teensy_3_1.D0, Componente2.TXD
  N5: Teensy_3_1.D1, Componente2.RXD
  N6: Teensy_3_1.D2, Componente3.STBY
  N7: Teensy_3_1.D3, Componente3.PWMA
  N8: Teensy_3_1.D4, Componente3.PWMB
  N9: Teensy_3_1.D5, Componente3.AIN2
  N10: Teensy_3_1.D6, Componente3.AIN1
  N11: Teensy_3_1.D7, Componente3.BIN1
  N12: Teensy_3_1.D8, Componente3.BIN2
  N13: Teensy_3_1.A3/D17, S1.pin11
  N14: Teensy_3_1.A4/D18, S1.pin10
  N15: Teensy_3_1.A5/D19, S1.pin9
  N16: Teensy_3_1.A6/D20, S1.pin8
  N17: Teensy_3_1.A7/D21, S1.pin7
  N18: Teensy_3_1.A8/D22, S1.pin4, S1.pin6
  N19: S1.pin24, S1.pin25
